# Fritzing sketch Untitled Sketch (saved by Fritzing 0.9.4)

parts:
  Part1 = Soil Moisture Sensor  # not connected
  Part2 = Soil Moisture Sensor  # not connected
  Part3 = Soil Moisture Sensor  # not connected
  Part4 = Soil Moisture Sensor  # not connected
  Part5 = Arduino Uno (Rev3)
  U1 = 4-Channel 5v Relay Shield [package=relay-4ch5v10a]

nets:
  N1: Part5.D2, U1.IN1
  N2: Part5.D3_PWM, U1.IN2
  N3: Part5.D4, U1.IN3
  N4: Part5.D5_PWM, U1.IN4
  5V: Part5.5V, U1.VCC
  GND: Part5.GND, U1.GND

custom parts:
  4-Channel 5v Relay Shield: 4 Channel 5v Relay Shield w. 2x SPD-06VDC-SD-C
